// Logisim project CPU_v2.circ as structural Verilog: 3 circuits, main circuit main
module main (
  input  in_1
);

  wire adder_1_cout, ALU_A_Sign, ALU_B_Sign, ALU_Carry, ALU_Carry_IN, ALU_OverFlow, ALU_Zero, and_1_out,
       clock_1_out, clock_2_out, clock_3_out, clock_5_out, clock_6_out, clock_7_out, CondMatch, d_ff_1_q,
       d_ff_2_q, decoder_1_out1, decoder_1_out2, decoder_1_out3, decoder_1_out4, decoder_1_out5,
       decoder_1_out6, decoder_1_out7, decoder_2_out0, decoder_2_out1, decoder_2_out2, decoder_2_out3,
       decoder_2_out4, decoder_2_out5, decoder_2_out6, decoder_2_out7, decoder_3_out0, decoder_3_out1,
       decoder_3_out2, decoder_3_out3, decoder_3_out4, decoder_3_out5, decoder_3_out6, decoder_3_out7,
       Flags_Carry, Flags_OutSign, Flags_Overflow, flags_swap, Flags_Zero, multiplexer_4_out,
       multiplexer_7_out, nor_1_out, nor_2_out, not_1_out, not_2_out, not_3_out, not_4_out, op2_is_imm,
       or_1_out, or_2_out, or_3_out, por_1_out, R, writeback_alu, xor_1_out, xor_2_out, xor_3_out;
  wire [0:0] clock_4_out;
  wire [1:0] COp, PcMode, SOp;
  wire [2:0] Immediate;
  wire [3:0] LOp, multiplexer_1_out, WA_RA1;
  wire [4:0] AluOp;
  wire [6:0] multiplexer_3_out, pla_decoder_lop_1_result;
  wire [7:0] ALU, ALU_Result, bit_extender_1_out, controlled_buffer_1_out, R0, R1, R2, R3, R4, R5, R6, RD1,
       RD2, RD2_out, RD3, register_2_q, rom_1_data;
  wire [15:0] adder_2_out, adder_3_out, bit_extender_2_out, multiplexer_8_out, PcReg;

  POR por_1 (.out(por_1_out));
  // Probe on R0
  // Probe on R1
  // Probe on R2
  // Probe on R3
  // Probe on R4
  // Probe on R5
  // Probe on R6
  // Probe on {R1, R0}
  // Probe on {R3, R2}
  // Probe on {R5, R4}
  // Probe on {R2, R1, R0}
  // Probe on {R5, R4, R3}
  LedBar #(.matrixcols(5)) ledbar_1 (
    .led0(AluOp[4]), .led1(AluOp[3]), .led2(AluOp[2]), .led3(AluOp[1]), .led4(AluOp[0]));
  Clock clock_1 (.out(clock_1_out));
  Multiplexer #(.width(4)) multiplexer_1 (
    .in0({ALU_OverFlow, ALU[7], ALU_Zero, ALU_Carry}), .in1(RD1[3:0]), .out(multiplexer_1_out),
    .sel(flags_swap));
  and and_1 (and_1_out, writeback_alu, ~AluOp[4]);  // AND_Gate
  D_Flip_Flop d_ff_1 (.D(por_1_out), .clk(clock_1_out), .Q(d_ff_1_q), .preset(por_1_out));  // open: Qn, reset
  // Probe on R0
  // Probe on R1
  // Probe on R2
  // Probe on R3
  // Probe on R4
  // Probe on R5
  // Probe on R6
  // Probe on {R1, R0}
  // Probe on {R3, R2}
  // Probe on {R5, R4}
  Register #(.width(4)) Flags (
    .D(multiplexer_1_out), .en(and_1_out), .clk(clock_2_out),
    .Q({Flags_Overflow, Flags_OutSign, Flags_Zero, Flags_Carry}));  // open: clr
  Clock clock_2 (.out(clock_2_out));
  D_Flip_Flop d_ff_2 (.D(d_ff_1_q), .clk(clock_1_out), .Q(d_ff_2_q), .preset(por_1_out));  // open: Qn, reset
  // Probe on {R2, R1, R0}
  // Probe on {R5, R4, R3}
  LedBar #(.matrixcols(2)) ledbar_2 (.led0(COp[1]), .led1(COp[0]));
  AluDecoder aludecoder_1 (.F(AluOp), .CondMatch(CondMatch), .COp(COp), .SOp(SOp), .InvRHS(LOp));
  D_Flip_Flop d_ff_3 (.D(d_ff_2_q), .clk(clock_1_out), .Q(R), .preset(por_1_out));  // open: Qn, reset
  not not_1 (not_1_out, WA_RA1[3]);
  Decoder #(.select(3)) decoder_1 (
    .out1(decoder_1_out1), .out2(decoder_1_out2), .out3(decoder_1_out3), .out4(decoder_1_out4),
    .out5(decoder_1_out5), .out6(decoder_1_out6), .out7(decoder_1_out7), .sel(WA_RA1[2:0]), .en(not_1_out));  // open: out0
  assign bit_extender_1_out = {{4{1'b0}}, {Flags_Overflow, Flags_OutSign, Flags_Zero, Flags_Carry}};  // Bit_Extender bit_extender_1
  LedBar #(.matrixcols(2)) ledbar_3 (.led0(SOp[1]), .led1(SOp[0]));
  LedBar ledbar_4 (
    .led0(controlled_buffer_1_out[7]), .led1(controlled_buffer_1_out[6]), .led2(controlled_buffer_1_out[5]),
    .led3(controlled_buffer_1_out[4]), .led4(controlled_buffer_1_out[3]), .led5(controlled_buffer_1_out[2]),
    .led6(controlled_buffer_1_out[1]), .led7(controlled_buffer_1_out[0]));
  assign controlled_buffer_1_out = writeback_alu ? ALU_Result : 8'bz;  // Controlled_Buffer controlled_buffer_1
  assign controlled_buffer_1_out = not_2_out ? RD2_out : 8'bz;  // Controlled_Buffer controlled_buffer_2
  Multiplexer #(.width(8)) multiplexer_2 (.in0(ALU), .in1(bit_extender_1_out), .out(ALU_Result), .sel(flags_swap));
  Multiplexer #(.select(2), .width(8)) multiplexer_3 (
    .in0({8{1'b0}}), .in1(RD1), .in2({RD1[6:0], ALU_Carry_IN}), .in3({ALU_Carry_IN, RD1[7:1]}),
    .out({ALU_A_Sign, multiplexer_3_out}), .sel(SOp));
  Clock clock_3 (.out(clock_3_out));
  Register u_R6 (.D(controlled_buffer_1_out), .en(decoder_1_out7), .clk(clock_3_out), .Q(R6));  // open: clr
  Register u_R5 (.D(controlled_buffer_1_out), .en(decoder_1_out6), .clk(clock_3_out), .Q(R5));  // open: clr
  Register u_R4 (.D(controlled_buffer_1_out), .en(decoder_1_out5), .clk(clock_3_out), .Q(R4));  // open: clr
  Register u_R3 (.D(controlled_buffer_1_out), .en(decoder_1_out4), .clk(clock_3_out), .Q(R3));  // open: clr
  Register u_R2 (.D(controlled_buffer_1_out), .en(decoder_1_out3), .clk(clock_3_out), .Q(R2));  // open: clr
  Register u_R1 (.D(controlled_buffer_1_out), .en(decoder_1_out2), .clk(clock_3_out), .Q(R1));  // open: clr
  Register u_R0 (.D(controlled_buffer_1_out), .en(decoder_1_out1), .clk(clock_3_out), .Q(R0));  // open: clr
  not not_2 (not_2_out, writeback_alu);
  LedBar #(.matrixcols(4)) ledbar_5 (.led0(LOp[3]), .led1(LOp[2]), .led2(LOp[1]), .led3(LOp[0]));
  Decoder #(.enable("false"), .select(3)) decoder_2 (
    .out0(decoder_2_out0), .out1(decoder_2_out1), .out2(decoder_2_out2), .out3(decoder_2_out3),
    .out4(decoder_2_out4), .out5(decoder_2_out5), .out6(decoder_2_out6), .out7(decoder_2_out7),
    .sel(WA_RA1[2:0]));
  PLA_Decoder_LOp pla_decoder_lop_1 (
    .LOp(LOp), .RD2(RD2[3:0]), .RD1(RD1[3:0]), .Swap(flags_swap), .result(pla_decoder_lop_1_result[3:0]));
  PLA_Decoder_LOp pla_decoder_lop_2 (
    .LOp(LOp), .RD2(RD2[7:4]), .RD1(RD1[7:4]), .result({ALU_B_Sign, pla_decoder_lop_1_result[6:4]}));  // open: Swap
  assign RD1 = decoder_2_out6 ? R5 : 8'bz;  // Controlled_Buffer controlled_buffer_3
  assign RD1 = decoder_2_out5 ? R4 : 8'bz;  // Controlled_Buffer controlled_buffer_4
  assign RD1 = decoder_2_out3 ? R2 : 8'bz;  // Controlled_Buffer controlled_buffer_5
  assign RD1 = decoder_2_out2 ? R1 : 8'bz;  // Controlled_Buffer controlled_buffer_6
  Multiplexer #(.select(2)) multiplexer_4 (
    .in0(ALU_Carry_IN), .in1(ALU_Carry_IN), .in2(1'b0), .in3(1'b0), .out(multiplexer_4_out), .sel(SOp));
  Adder adder_1 (
    .a({ALU_A_Sign, multiplexer_3_out}), .b({ALU_B_Sign, pla_decoder_lop_1_result}), .out(ALU),
    .cin(multiplexer_4_out), .cout(adder_1_cout));
  Decoder #(.enable("false"), .select(3)) decoder_3 (
    .out0(decoder_3_out0), .out1(decoder_3_out1), .out2(decoder_3_out2), .out3(decoder_3_out3),
    .out4(decoder_3_out4), .out5(decoder_3_out5), .out6(decoder_3_out6), .out7(decoder_3_out7),
    .sel(Immediate));
  assign RD1 = decoder_2_out7 ? R6 : 8'bz;  // Controlled_Buffer controlled_buffer_7
  assign RD1 = decoder_2_out4 ? R3 : 8'bz;  // Controlled_Buffer controlled_buffer_8
  assign RD1 = decoder_2_out1 ? R0 : 8'bz;  // Controlled_Buffer controlled_buffer_9
  assign RD1 = decoder_2_out0 ? {8{1'b0}} : 8'bz;  // Controlled_Buffer controlled_buffer_10
  LedBar ledbar_6 (
    .led0(RD1[7]), .led1(RD1[6]), .led2(RD1[5]), .led3(RD1[4]), .led4(RD1[3]), .led5(RD1[2]), .led6(RD1[1]),
    .led7(RD1[0]));
  or or_1 (or_1_out, ~Flags_Carry, Flags_Zero);  // OR_Gate
  xor xor_1 (xor_1_out, Flags_OutSign, Flags_Overflow);
  Multiplexer #(.select(2)) multiplexer_5 (
    .in0(1'b0), .in1(1'b1), .in2(Flags_Carry), .in3(Flags_Carry), .out(ALU_Carry_IN), .sel(COp));
  Multiplexer #(.select(2)) multiplexer_6 (
    .in0(adder_1_cout), .in1(adder_1_cout), .in2(RD1[7]), .in3(RD1[0]), .out(ALU_Carry), .sel(SOp));
  assign RD2 = decoder_3_out7 ? R6 : 8'bz;  // Controlled_Buffer controlled_buffer_11
  assign RD2 = decoder_3_out6 ? R5 : 8'bz;  // Controlled_Buffer controlled_buffer_12
  assign RD2 = decoder_3_out5 ? R4 : 8'bz;  // Controlled_Buffer controlled_buffer_13
  assign RD2 = decoder_3_out4 ? R3 : 8'bz;  // Controlled_Buffer controlled_buffer_14
  assign RD2 = decoder_3_out3 ? R2 : 8'bz;  // Controlled_Buffer controlled_buffer_15
  assign RD2 = decoder_3_out2 ? R1 : 8'bz;  // Controlled_Buffer controlled_buffer_16
  assign RD2 = decoder_3_out1 ? R0 : 8'bz;  // Controlled_Buffer controlled_buffer_17
  assign RD2 = decoder_3_out0 ? {8{1'b0}} : 8'bz;  // Controlled_Buffer controlled_buffer_18
  not not_3 (not_3_out, op2_is_imm);
  or or_2 (or_2_out, xor_1_out, Flags_Zero);
  LedBar ledbar_7 (
    .led0(RD2[7]), .led1(RD2[6]), .led2(RD2[5]), .led3(RD2[4]), .led4(RD2[3]), .led5(RD2[2]), .led6(RD2[1]),
    .led7(RD2[0]));
  assign RD2_out = not_3_out ? RD2 : 8'bz;  // Controlled_Buffer controlled_buffer_19
  assign RD2_out = op2_is_imm ? {AluOp[3:0], AluOp[4], Immediate} : 8'bz;  // Controlled_Buffer controlled_buffer_20
  nor nor_1 (nor_1_out, ALU[0], ALU[1], ALU[2], ALU[3]);
  nor nor_2 (nor_2_out, ALU[4], ALU[5], ALU[6], ALU[7]);
  assign RD3 = decoder_3_out6 ? R6 : 8'bz;  // Controlled_Buffer controlled_buffer_21
  assign RD3 = decoder_3_out5 ? R5 : 8'bz;  // Controlled_Buffer controlled_buffer_22
  assign RD3 = decoder_3_out4 ? R4 : 8'bz;  // Controlled_Buffer controlled_buffer_23
  assign RD3 = decoder_3_out3 ? R3 : 8'bz;  // Controlled_Buffer controlled_buffer_24
  assign RD3 = decoder_3_out2 ? R2 : 8'bz;  // Controlled_Buffer controlled_buffer_25
  assign RD3 = decoder_3_out1 ? R1 : 8'bz;  // Controlled_Buffer controlled_buffer_26
  assign RD3 = decoder_3_out0 ? R0 : 8'bz;  // Controlled_Buffer controlled_buffer_27
  assign RD3 = decoder_3_out7 ? {8{1'b0}} : 8'bz;  // Controlled_Buffer controlled_buffer_28
  LedBar ledbar_8 (
    .led0(RD3[7]), .led1(RD3[6]), .led2(RD3[5]), .led3(RD3[4]), .led4(RD3[3]), .led5(RD3[2]), .led6(RD3[1]),
    .led7(RD3[0]));
  Multiplexer #(.select(3)) multiplexer_7 (
    .in0(1'b1), .in1(Flags_Carry), .in2(Flags_Zero), .in3(Flags_OutSign), .in4(Flags_Overflow),
    .in5(or_1_out), .in6(xor_1_out), .in7(or_2_out), .out(multiplexer_7_out), .sel(AluOp[3:1]));
  and and_2 (ALU_Zero, nor_1_out, nor_2_out);
  xor xor_2 (xor_2_out, ALU[7], ALU_A_Sign);
  xor xor_3 (xor_3_out, ALU[7], ALU_B_Sign);
  xor xor_4 (CondMatch, multiplexer_7_out, AluOp[0]);
  and and_3 (ALU_OverFlow, xor_2_out, xor_3_out);
  Clock clock_4 (.out(clock_4_out[0]));
  ROM #(.addrWidth(16)) rom_1 (.addr({PcReg[15:1], clock_4_out[0]}), .data(rom_1_data));
  Adder #(.width(16)) adder_2 (.a(PcReg), .b(16'h2), .out(adder_2_out));  // open: cin, cout
  Adder #(.width(16)) adder_3 (.a(PcReg), .b(bit_extender_2_out), .out(adder_3_out));  // open: cin, cout
  assign bit_extender_2_out = {{8{RD2_out[7]}}, RD2_out};  // Bit_Extender bit_extender_2
  Multiplexer #(.select(2), .width(16)) multiplexer_8 (
    .in0(adder_2_out), .in1(adder_3_out), .in2({RD3, RD2}), .out(multiplexer_8_out), .sel(PcMode));  // open: in3
  Register #(.width(16)) register_1 (.D(multiplexer_8_out), .clk(clock_5_out), .Q(PcReg), .clr(R));  // open: en
  Clock clock_5 (.out(clock_5_out));
  Register #(.trigger("high")) register_2 (.D(rom_1_data), .clk(clock_6_out), .Q(register_2_q));  // open: en, clr
  Clock clock_6 (.out(clock_6_out));
  Clock clock_7 (.out(clock_7_out));
  assign {AluOp[3:0], AluOp[4], Immediate, WA_RA1, op2_is_imm, writeback_alu, PcMode} = not_4_out ? {rom_1_data, register_2_q} : 16'bz;  // Controlled_Buffer controlled_buffer_29
  not not_4 (not_4_out, or_3_out);
  or or_3 (or_3_out, clock_7_out, in_1);
  Pull_Resistor pull_resistor_1 (.node(AluOp[3]));
  Pull_Resistor pull_resistor_2 (.node(AluOp[2]));
  // Probe on {AluOp[3:0], AluOp[4], Immediate, WA_RA1, op2_is_imm, writeback_alu, PcMode}
  Pull_Resistor pull_resistor_3 (.node(AluOp[1]));
  Pull_Resistor pull_resistor_4 (.node(AluOp[0]));
  Pull_Resistor pull_resistor_5 (.node(AluOp[4]));
  Pull_Resistor pull_resistor_6 (.node(Immediate[2]));
  LedBar #(.matrixcols(16)) ledbar_9 (
    .led0(AluOp[3]), .led1(AluOp[2]), .led2(AluOp[1]), .led3(AluOp[0]), .led4(AluOp[4]), .led5(Immediate[2]),
    .led6(Immediate[1]), .led7(Immediate[0]), .led8(WA_RA1[3]), .led9(WA_RA1[2]), .led10(WA_RA1[1]),
    .led11(WA_RA1[0]), .led12(op2_is_imm), .led13(writeback_alu), .led14(PcMode[1]), .led15(PcMode[0]));
  Pull_Resistor pull_resistor_7 (.node(Immediate[1]));
  Pull_Resistor pull_resistor_8 (.node(Immediate[0]));
  Pull_Resistor pull_resistor_9 (.node(WA_RA1[3]));
  Pull_Resistor pull_resistor_10 (.node(WA_RA1[2]));
  Pull_Resistor pull_resistor_11 (.node(WA_RA1[1]));
  Pull_Resistor pull_resistor_12 (.node(WA_RA1[0]));
  Pull_Resistor pull_resistor_13 (.node(op2_is_imm));
  Pull_Resistor pull_resistor_14 (.node(writeback_alu));
  Pull_Resistor pull_resistor_15 (.node(PcMode[1]));
  Pull_Resistor pull_resistor_16 (.node(PcMode[0]));

  // Other names for the same wires on the sheet: RA2[3:0] = {AluOp[4], Immediate}; ALU_Out_Sign = ALU[7];
  //   Immediate[7:3] = {AluOp[3:0], AluOp[4]}; RD32[15:0] = {RD3, RD2}

  // Notes on the sheet:
  //   contents of rom_1 (hex, n*v repeats v):
  //   0 18 1 20 2 30 3 40 4 50 5 60 6 70 9 18 c0 14 1 18 29 24 39 34 49 44 59 54 0 28 0 58 69 24 79 34 89
  //   44 99 54 0 38 0 48 0 18 0 0 1 18 c8 28 c9 38 23 a4 39 44 a9 54 29 64 b9 74 0 48 0 58 c9 28 23 a4 39
  //   44 a9 54 29 64 b9 74 0 58 0 68 c8 38 23 a4 39 44 a9 54 29 64 b9 74 0 68 0 78 0 18 0 28 0 38 0 0 1 18
  //   81 28 7f 38 23 a4 c9 44 e9 54 d9 64 f9 74 0 48 0 58 81 38 23 a4 c9 44 e9 54 d9 64 f9 74 0 58 0 68 7f
  //   28 23 a4 c9 44 e9 54 d9 64 f9 74 0 68 0 78 0 18 0 28 0 38 0 0 3 18 2a 28 1 48 fa 58 2 68 2 34 24 14
  //   4e 54 5 1 0 28 0 48 0 58 0 68 0 38 0 0 1 18 d 28 9 38 4c 48 2a 58 8f 68 80 78 22 94 3a 14 23 94 3b
  //   14 24 94 3c 14 25 94 3d 14 26 94 3e 14 27 94 3f 14 0 78 7 60 7 50 7 40 7 30 7 20 7 10 0 0 1 38 f0 78
  //   1 50 2 60 3 10 4 20 5 34 16 44 2 68 2e 74 7 1 0 78 7 60 7 50 7 40 7 30 0 9
endmodule

module AluDecoder (
  input  [4:0] F,
  input  CondMatch,
  output [1:0] COp,
  output [1:0] SOp,
  output [3:0] InvRHS
);

  wire and_1_out, and_2_out, and_3_out, and_4_out, and_5_out, and_6_out, and_7_out, and_8_out, and_10_out,
       and_11_out, and_12_out, and_13_out, and_14_out, and_15_out, and_16_out, and_17_out, and_18_out,
       and_19_out, and_20_out, and_21_out, and_22_out, and_23_out, not_1_out, not_2_out, not_3_out,
       not_4_out, not_5_out, not_6_out;

  not not_1 (not_1_out, F[4]);
  not not_2 (not_2_out, F[3]);
  not not_3 (not_3_out, F[2]);
  not not_4 (not_4_out, F[1]);
  not not_5 (not_5_out, F[0]);
  not not_6 (not_6_out, CondMatch);
  and and_1 (and_1_out, not_1_out, not_3_out, F[0]);
  and and_2 (and_2_out, not_1_out, not_2_out, F[1], F[0]);
  and and_3 (and_3_out, not_1_out, F[3], not_3_out, F[1]);
  and and_4 (and_4_out, not_1_out, not_2_out, not_3_out, F[1]);
  and and_5 (and_5_out, not_1_out, not_2_out, F[0]);
  and and_6 (and_6_out, not_1_out, not_3_out, F[0]);
  and and_7 (and_7_out, not_1_out, not_2_out, F[2], F[1]);
  and and_8 (and_8_out, not_1_out, F[3], not_3_out);
  and and_9 (SOp[0], not_1_out, not_3_out);
  and and_10 (and_10_out, not_2_out, not_3_out, not_4_out);
  and and_11 (and_11_out, F[3], F[2], not_4_out);
  and and_12 (and_12_out, F[3], F[2], not_5_out);
  and and_13 (and_13_out, not_1_out, not_2_out, not_3_out, F[1]);
  and and_14 (and_14_out, not_1_out, F[3], F[2], not_5_out);
  and and_15 (and_15_out, F[4], not_6_out);
  and and_16 (and_16_out, not_1_out, F[3], F[1], F[0]);
  and and_17 (and_17_out, not_1_out, not_2_out, not_4_out);
  and and_18 (and_18_out, F[4], CondMatch);
  and and_19 (and_19_out, not_1_out, F[3], F[2], not_5_out);
  and and_20 (and_20_out, not_1_out, F[3], F[2], F[1]);
  and and_21 (and_21_out, not_1_out, not_2_out, not_3_out, F[1]);
  and and_22 (and_22_out, not_1_out, F[2], not_4_out, not_5_out);
  and and_23 (and_23_out, not_1_out, not_2_out, F[2], not_4_out);
  or or_1 (COp[1], and_1_out, and_2_out, and_3_out);
  or or_2 (COp[0], and_4_out, and_5_out, and_6_out);
  or or_3 (SOp[1], and_7_out, and_8_out);
  or or_4 (InvRHS[3], and_10_out, and_11_out, and_12_out, F[4]);
  or or_5 (InvRHS[2], and_13_out, and_14_out, and_15_out, and_16_out);
  or or_6 (InvRHS[1], and_17_out, and_18_out, and_19_out, and_20_out);
  or or_7 (InvRHS[0], and_21_out, and_22_out, and_23_out);
endmodule

module PLA_Decoder_LOp (
  input  [3:0] LOp,
  input  [3:0] RD2,
  input  [3:0] RD1,
  output Swap,
  output [3:0] result
);

  PLA #(.in_width(12), .out_width(1), .\table ("xxxxxxxx1111 1")) pla_1 (.in({RD1, RD2, LOp}), .out(Swap));
  PLA #(.in_width(12), .out_width(1), .\table ("xxx0xxx0xxx1 1\nxxx0xxx1xx1x 1\nxxx1xxx0x1xx 1\nxxx1xxx11xxx 1")) pla_2 (
    .in({RD1, RD2, LOp}), .out(result[0]));
  PLA #(.in_width(12), .out_width(1), .\table ("xx0xxx0xxxx1 1\nxx0xxx1xxx1x 1\nxx1xxx0xx1xx 1\nxx1xxx1x1xxx 1")) pla_3 (
    .in({RD1, RD2, LOp}), .out(result[1]));
  PLA #(.in_width(12), .out_width(1), .\table ("x0xxx0xxxxx1 1\nx0xxx1xxxx1x 1\nx1xxx0xxx1xx 1\nx1xxx1xx1xxx 1")) pla_4 (
    .in({RD1, RD2, LOp}), .out(result[2]));
  PLA #(.in_width(12), .out_width(1), .\table ("0xxx0xxxxxx1 1\n0xxx1xxxxx1x 1\n1xxx0xxxx1xx 1\n1xxx1xxx1xxx 1")) pla_5 (
    .in({RD1, RD2, LOp}), .out(result[3]));
endmodule
